# Fritzing sketch tempcontroller (saved by Fritzing 0.7.7b)
breadboards: 1

parts:
  S2 = Pushbutton [package="[THT]"]
  S3 = Pushbutton [package="[THT]"]
  Arduino1 = Arduino
  LED1 = LED - 5mm [color="Red (633nm)" package="5 mm [THT]"]
  LED2 = LED - 5mm [color="Red (633nm)" package="5 mm [THT]"]
  LED3 = LED - 5mm [color="Red (633nm)" package="5 mm [THT]"]
  LED4 = LED - 5mm [color="Red (633nm)" package="5 mm [THT]"]
  LED5 = LED - 5mm [color="Red (633nm)" package="5 mm [THT]"]
  LED6 = LED - 5mm [color="Red (633nm)" package="5 mm [THT]"]
  LED7 = LED - 5mm [color="Red (633nm)" package="5 mm [THT]"]
  R2 = Resistor [tolerance=±5% resistance=220 package=THT]
  R3 = Resistor [tolerance=±5% resistance=220 package=THT]
  R4 = Resistor [tolerance=±5% resistance=220 package=THT]
  R5 = Resistor [tolerance=±5% resistance=220 package=THT]
  R6 = Resistor [tolerance=±5% resistance=220 package=THT]
  R7 = Resistor [tolerance=±5% resistance=220 package=THT]
  R8 = Resistor [tolerance=±5% resistance=220 package=THT]
  T1 = LM35 Temperature Sensor [package="TO92 [THT]"]
  R9 = Resistor [tolerance=±5% resistance=220 package=THT]
  R10 = Resistor [tolerance=±5% resistance=220 package=THT]
  R11 = Resistor [tolerance=±5% resistance=220 package=THT]
  K1 = Relay [part_number=FRS1B-S package=THT]
  U1 = atmega328 [package=dip]  # not connected

nets (from the breadboard view):
  N1: S2.Pin_1, S2.Pin_2, Arduino1.D12, R9.Pin_1
  N2: S2.Pin_3, S2.Pin_4, S3.Pin_3, S3.Pin_4, Arduino1.+5V, T1.Vout
  N3: S3.Pin_1, S3.Pin_2, Arduino1.D11, R10.Pin_1
  N4: Arduino1.GND, R2.Pin_0, R3.Pin_0, R4.Pin_0, R5.Pin_0, R6.Pin_0, R7.Pin_0, R8.Pin_0, T1.+Vs, R9.Pin_0, R10.Pin_0, R11.Pin_0, K1.B
  N5: Arduino1.D10, T1.GND
  N6: Arduino1.D9, K1.A
  N7: Arduino1.D8, LED1.cathode
  N8: Arduino1.D7, LED2.cathode
  N9: Arduino1.D6, LED7.cathode
  N10: Arduino1.D5, LED3.cathode
  N11: Arduino1.D4, LED4.cathode
  N12: Arduino1.D3, LED5.cathode
  N13: Arduino1.D2, LED6.cathode
  N14: LED1.anode, R2.Pin_1
  N15: LED2.anode, R3.Pin_1
  N16: LED3.anode, R5.Pin_1
  N17: LED4.anode, R6.Pin_1
  N18: LED5.anode, R7.Pin_1
  N19: LED6.anode, R8.Pin_1
  N20: LED7.anode, R4.Pin_1

notes:
  resistor pull down on temp sensor?
